# Fritzing sketch TEAM11-circuit diagram (saved by Fritzing 0.9.3b)
breadboards: 3

parts:
  L298N1 = L298N DC motor driver
  U1 = GAS_SENSOR [package=mq-3]
  M3 = DC Motor  # not connected
  M4 = DC Motor  # not connected
  VCC1 = Battery
  ESP32_-_Back1 = ESP32 - CAM
  Part1 = Arduino Mega ADK (Rev3)
  Mod2 = flyskyr6b
  U2 = ESP8266 NodeMCU LoLin module

nets:
  GND: L298N1.GND, U1.H1, ESP32_-_Back1.GND, Part1.GND, Mod2.BAT+, U2.GND
  5V: L298N1.5V, U1.B1, VCC1.-, Part1.IOREF, Part1.5V, Mod2.BIND, U2.Vin
  N1: L298N1.IN1, Part1.D2_PWM
  N2: L298N1.IN2, Part1.D3_PWM
  N3: L298N1.IN3, Part1.D4_PWM
  N4: L298N1.IN4, Part1.D5_PWM
  N5: U1.A1, Part1.A8
  N6: VCC1.+, Part1.VIN
  3.3V: ESP32_-_Back1.3.3V, U2.3V3
  N7: ESP32_-_Back1.GPIO3_/_RX, U2.TX
  N8: ESP32_-_Back1.GPIO1_/_TX, U2.RX
  N9: Part1.D43, Mod2.CH4
  N10: Part1.D45, Mod2.CH3
  N11: Part1.D47, Mod2.CH2
  N12: Part1.D49, Mod2.CH1

custom parts:
  L298N DC motor driver: 2x DC motor driver with 78M05 positive voltage regulator (7..35 V) L298N: max 46 V, 2 A Set 5 V Enable jumper to enable 5 V regultor (needed for the L298N) and +5 V output at screw terminal or supply external +5 V at screw terminal Set ENA and/or ENB to +5 V to enable motor permanently or supply ENA and/or ENB with PWM signal IN1 and IN2 set rotation directory for motor A (OUT1/OUT2) IN2 and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
  ESP32 - CAM: The ESP32-CAM has a very competitive small-size camera module that can operate independently as a minimum system with a footprint of only 27*40.5*4.5mm and a deep sleep current of up to 6mA.
  flyskyr6b: flysky r6b 6ch rc receiver module. Pcb view is 3*7 header pins, 3 female headers will let the board plug in to the receiver, or connect via wires as you choose.
  ESP8266 NodeMCU LoLin module: ESP8266 based NodeMCU
